# Fritzing sketch ESP 8266 - RF and LED (saved by Fritzing 0.9.3b)

parts:
  ANT1 = Antenna
  U3 = NodeMCU V1.0
  U5 = RF 315/433 Transmitter [package=rf-link_tx]
  part = LED - 3mm [color="Infrared (940nm)" package="3 mm [THT]"]
  2N2222 = TRANSISTOR_NPN [package=to-92]
  R1 = Resistor [tolerance=±5% resistance=1k package=THT]
  R2 = Resistor [tolerance=±5% resistance=100 package=THT]

nets:
  N1: ANT1.antenna_lead, U5.ANT
  N2: U3.D1, U5.DATA
  N3: U3.D2, R1.Pin_0
  GND: U3.GND, U5.GND, 2N2222.E
  VIN: U3.Vin, U5.+5V, R2.Pin_0
  N4: part.cathode, 2N2222.C
  N5: part.anode, R2.Pin_1
  N6: 2N2222.B, R1.Pin_1

notes:
  RF and LED Transmitter
  Green - Gnd
  Yellow - D2
  Red - Vin ( 5V )
  Black - Antenna

custom parts:
  NodeMCU V1.0: ESP8266 based NodeMCU
  RF 315/433 Transmitter: 315/433 Mhz RF Transmitter
